# Fritzing sketch nano_receiver (saved by Fritzing 0.7.1b)

parts:
  Nano1 = Arduino Nano v2.3
  Part1 = XBee Explorer Regulated
  J1 = Basic Servo
  J2 = Basic Servo  # not connected
  J3 = Basic Servo  # not connected
  J4 = Basic Servo  # not connected
  J5 = Basic Servo  # not connected
  J6 = Basic Servo  # not connected

nets:
  N1: Nano1.D1TX, Part1.DIN
  N2: Nano1.D0RX, Part1.DOUT
  GND: Nano1.GND, Part1.GND, J1.gnd
  +5V: Nano1.+5V, Part1.5V
