# Fritzing sketch serial_ppm_rx (saved by Fritzing 0.7.1b)
breadboards: 1

parts:
  Arduino1 = Arduino
  Part1 = XBee Explorer Regulated
  U1 = XBee  # not connected
  J1 = Basic Servo
  J2 = Basic Servo
  J3 = Basic Servo
  J4 = Basic Servo
  J5 = Basic Servo
  J6 = Basic Servo
  J7 = Basic Servo
  J8 = Basic Servo

nets:
  N1: Arduino1.D7, J3.pulse
  N2: Arduino1.D6, J4.pulse
  N3: Arduino1.D5, J5.pulse
  N4: Arduino1.D4, J6.pulse
  N5: Arduino1.D3, J7.pulse
  N6: Arduino1.D2, J8.pulse
  N7: Arduino1.D1TX, Part1.DIN
  N8: Arduino1.D0RX, Part1.DOUT
  VCC: Arduino1.+5V, Part1.5V, J1.vcc, J2.vcc, J4.vcc, J6.vcc, J7.vcc, J8.vcc
  GND: Arduino1.GND, Part1.GND, J1.gnd, J2.gnd, J3.gnd, J4.gnd, J5.gnd, J7.gnd, J8.gnd
